// Logisim project alu_6.circ as structural Verilog: 1 circuit, main circuit main
module main (
  input  [3:0] in_1
);

  wire clock_1_out, demultiplexer_2_out0, demultiplexer_2_out1, demultiplexer_2_out2, demultiplexer_2_out3,
       not_1_out, or_1_out;
  wire [1:0] ram_1_data_2;
  wire [7:0] adder_1_out, demultiplexer_1_out0, demultiplexer_1_out1, demultiplexer_1_out2,
       demultiplexer_1_out3, multiplexer_1_out, multiplexer_2_out, multiplexer_3_out, ram_2_data,
       register_1_q, register_2_q, register_3_q, register_4_q;
  wire [15:0] ram_1_data;

  Clock clock_1 (.out(clock_1_out));
  RAM #(.addrWidth(4), .dataWidth(16)) ram_1 (
    .addr(in_1), .data({ram_1_data[15:4], ram_1_data_2, ram_1_data[1:0]}), .clk(clock_1_out));  // open: sel, ld, clr
  // Probe on ram_1_data[10:8]
  // Probe on ram_1_data[14]
  // Probe on ram_1_data[7:6]
  // Probe on ram_1_data[13]
  // Probe on ram_1_data[5:4]
  // Probe on ram_1_data[12]
  // Probe on ram_1_data_2
  not not_1 (not_1_out, ram_1_data[12]);
  RAM #(.addrWidth(3)) ram_2 (
    .addr(ram_1_data[10:8]), .data(ram_2_data), .sel(not_1_out), .clk(clock_1_out), .ld(ram_1_data[14]));  // open: clr
  assign ram_2_data = ram_1_data[13] ? multiplexer_1_out : 8'bz;  // Controlled_Buffer controlled_buffer_1
  assign ram_2_data = ram_1_data[12] ? adder_1_out : 8'bz;  // Controlled_Buffer controlled_buffer_2
  Demultiplexer #(.select(2), .width(8)) demultiplexer_1 (
    .out0(demultiplexer_1_out0), .out1(demultiplexer_1_out1), .out2(demultiplexer_1_out2),
    .out3(demultiplexer_1_out3), .in(ram_2_data), .sel(ram_1_data[7:6]));  // open: en
  or or_1 (or_1_out, ram_1_data[14], ram_1_data[12]);
  Demultiplexer #(.select(2)) demultiplexer_2 (
    .out0(demultiplexer_2_out0), .out1(demultiplexer_2_out1), .out2(demultiplexer_2_out2),
    .out3(demultiplexer_2_out3), .in(or_1_out), .sel(ram_1_data[7:6]));  // open: en
  Register register_1 (
    .D(demultiplexer_1_out0), .en(demultiplexer_2_out0), .Q(register_1_q), .clk(clock_1_out));  // open: clr
  Register register_2 (
    .D(demultiplexer_1_out1), .en(demultiplexer_2_out1), .Q(register_2_q), .clk(clock_1_out));  // open: clr
  Register register_3 (
    .D(demultiplexer_1_out2), .en(demultiplexer_2_out2), .Q(register_3_q), .clk(clock_1_out));  // open: clr
  Register register_4 (
    .D(demultiplexer_1_out3), .en(demultiplexer_2_out3), .Q(register_4_q), .clk(clock_1_out));  // open: clr
  Multiplexer #(.select(2), .width(8)) multiplexer_1 (
    .in0(register_1_q), .in1(register_2_q), .in2(register_3_q), .in3(register_4_q), .out(multiplexer_1_out),
    .sel(ram_1_data[7:6]));  // open: en
  Multiplexer #(.select(2), .width(8)) multiplexer_2 (
    .in0(register_1_q), .in1(register_2_q), .in2(register_3_q), .in3(register_4_q), .out(multiplexer_2_out),
    .sel(ram_1_data[5:4]));  // open: en
  Multiplexer #(.select(2), .width(8)) multiplexer_3 (
    .in0(register_1_q), .in1(register_2_q), .in2(register_3_q), .in3(register_4_q), .out(multiplexer_3_out),
    .sel(ram_1_data_2));  // open: en
  Adder adder_1 (.a(multiplexer_2_out), .b(multiplexer_3_out), .out(adder_1_out));  // open: cin, cout
endmodule
