// Logisim project comp_2.circ as structural Verilog: 2 circuits, main circuit main
module main (
  input  in_1,
  input  Reset_PC
);

  wire clock_1_out;
  wire [2:0] undriven, undriven_2, undriven_3;
  wire [7:0] counter_1_q, register_file_1_read_data_1, register_file_1_read_data_2, undriven_4;
  wire [15:0] ram_1_data;

  Counter counter_1 (.Q(counter_1_q), .clk(clock_1_out), .clr(Reset_PC));  // open: load, D, count, carry
  Clock clock_1 (.out(clock_1_out));
  RAM #(.dataWidth(16)) ram_1 (.addr(counter_1_q), .data(ram_1_data), .clk(clock_1_out));  // open: sel, ld, clr
  Register_File register_file_1 (
    .Read_Address_1(undriven_2), .Read_Address_2(undriven), .Write_Address(undriven_3),
    .Write_Data(undriven_4), .Read_Write(in_1), .Clock(clock_1_out),
    .Read_Data_1(register_file_1_read_data_1), .Read_Data_2(register_file_1_read_data_2));
  // Probe on register_file_1_read_data_1
endmodule

module Register_File (
  input  [2:0] Read_Address_1,
  input  [2:0] Read_Address_2,
  input  [2:0] Write_Address,
  input  [7:0] Write_Data,
  input  Read_Write,
  input  Clock,
  output [7:0] Read_Data_1,
  output [7:0] Read_Data_2
);

  wire decoder_1_out1, decoder_1_out2, decoder_1_out3, decoder_1_out4, decoder_1_out5, decoder_1_out6,
       decoder_1_out7;
  wire [7:0] register_1_q, register_2_q, register_3_q, register_4_q, register_5_q, register_6_q,
       register_7_q, register_8_q;

  Decoder #(.select(3), .disabled(0)) decoder_1 (
    .out1(decoder_1_out1), .out2(decoder_1_out2), .out3(decoder_1_out3), .out4(decoder_1_out4),
    .out5(decoder_1_out5), .out6(decoder_1_out6), .out7(decoder_1_out7), .sel(Write_Address), .en(Read_Write));  // open: out0
  Register register_1 (.Q(register_1_q));  // open: D, en, clk, clr
  Register register_2 (.D(Write_Data), .en(decoder_1_out1), .Q(register_2_q), .clk(Clock));  // open: clr
  Register register_3 (.D(Write_Data), .en(decoder_1_out2), .Q(register_3_q), .clk(Clock));  // open: clr
  Register register_4 (.D(Write_Data), .en(decoder_1_out3), .Q(register_4_q), .clk(Clock));  // open: clr
  Register register_5 (.D(Write_Data), .en(decoder_1_out4), .Q(register_5_q), .clk(Clock));  // open: clr
  Register register_6 (.D(Write_Data), .en(decoder_1_out5), .Q(register_6_q), .clk(Clock));  // open: clr
  Register register_7 (.D(Write_Data), .en(decoder_1_out6), .Q(register_7_q), .clk(Clock));  // open: clr
  Register register_8 (.D(Write_Data), .en(decoder_1_out7), .Q(register_8_q), .clk(Clock));  // open: clr
  Multiplexer #(.select(3), .width(8), .enable("false")) multiplexer_1 (
    .in0(register_1_q), .in1(register_2_q), .in2(register_3_q), .in3(register_4_q), .in4(register_5_q),
    .in5(register_6_q), .in6(register_7_q), .in7(register_8_q), .out(Read_Data_1), .sel(Read_Address_1));
  Multiplexer #(.select(3), .width(8), .enable("false")) multiplexer_2 (
    .in0(register_1_q), .in1(register_2_q), .in2(register_3_q), .in3(register_4_q), .in4(register_5_q),
    .in5(register_6_q), .in6(register_7_q), .in7(register_8_q), .out(Read_Data_2), .sel(Read_Address_2));
endmodule
